# Fritzing sketch Untitled Sketch (saved by Fritzing 0.9.9b)
breadboards: 1

parts:
  DHT1 = DHT11 Humitidy and Temperature Sensor
  Part1 = MQ-7 breakout
  Mod1 = KY-026 Flame Sensor Module [package="Breakout board"]
  Mod2 = Raspberry Pi 4B
  buz1 = Piezo Buzzer

nets:
  VDD: DHT1.VDD, Part1.VCC, Mod1.+, Mod2.5V
  N1: DHT1.DATA, Mod2.GPIO18
  GND: DHT1.GND, Part1.GND, Mod1.G, Mod2.GND, buz1.pin_1
  N2: Part1.AO, Mod2.GPIO23
  N3: Mod1.D0, Mod2.GPIO24
  N4: Mod2.GPIO25, buz1.pin_2

custom parts:
  DHT11 Humitidy and Temperature Sensor: DHT11 Humidity and Temperature Sensor
  MQ-7 breakout: SKU: 101282
  KY-026 Flame Sensor Module: KY-026 Flame Sensor Module reacts in the presence of fire.
  Piezo Buzzer: Part from https://www.nutsvolts.com/magazine/article/november2012_SmileysWorkshop modified to be .3 in spacing to match the adafruit buzzer 5V breadboard friendly part.
